# Fritzing sketch CAVEDROP_32822RV2 (saved by Fritzing 1.0.2b)
circuit board: 7.53273cm x 5.57483cm

parts:
  LED1 = LED - 5mm [color="Red (633nm)" current=0.030A package="5 mm [THT]"]
  ON_1m_10m_1h = Piezoelectric Sensor
  ©aros_2024 = DIP Switch 4 Position [package=dipswitch-04]
  ZS-042_RTC1 = ZS-042 RTC Module
  VCC1 = Battery
  CaveDrop_32822rv = Arduino Pro Mini (5V)
  1MΩ = Resistor [tolerance=±5% resistance=1M package="0805 [SMD]"]
  SD_max_32GB1 = OpenLog

nets:
  GND: LED1.cathode, ON_1m_10m_1h.GND, ©aros_2024.5, ©aros_2024.6, ©aros_2024.7, ZS-042_RTC1.GND, VCC1.-, CaveDrop_32822rv.GND, 1MΩ.Pin_0, SD_max_32GB1.GND
  N1: LED1.anode, CaveDrop_32822rv.D2
  N2: ON_1m_10m_1h.VCC, CaveDrop_32822rv.A1, 1MΩ.Pin_1
  N3: ©aros_2024.1, VCC1.+
  N4: ©aros_2024.2, CaveDrop_32822rv.D3
  N5: ©aros_2024.3, CaveDrop_32822rv.D4
  N6: ©aros_2024.4, CaveDrop_32822rv.D5
  VCC: ©aros_2024.8, ZS-042_RTC1.VCC, CaveDrop_32822rv.VCC, SD_max_32GB1.VCC
  N7: ZS-042_RTC1.SDA, CaveDrop_32822rv.A4, CaveDrop_32822rv.A2
  N8: ZS-042_RTC1.SCL, CaveDrop_32822rv.A5, CaveDrop_32822rv.A3
  N9: CaveDrop_32822rv.RXI, SD_max_32GB1.TXO
  N10: CaveDrop_32822rv.TXO, SD_max_32GB1.RXI

notes:
  CaveDrop 32822rv
  © aros

custom parts:
  Piezoelectric Sensor: Piezoelectric sensor.
